// Logisim project Final_gnome_sort.circ as structural Verilog: 3 circuits, main circuit main
module main (
  input  \Сброс ,
  output [7:0] out_2
);

  wire and_1_out, and_2_out, and_3_out, and_4_out, not_1_out, or_1_out, or_2_out, or_3_out, or_4_out,
       \компаратор_1_out_4 , \компаратор_2_out_3 , \компаратор_2_out_4 , \компаратор_3_out_3 ,
       \компаратор_3_out_4 , \Тактовый_генератор_out ;
  wire [2:0] \Командный_регистр_q_2 , \Счетчик_команд_q ;
  wire [3:0] bit_extender_3_out, bit_extender_4_out, bit_extender_5_out, bit_extender_6_out,
       bit_extender_7_out;
  wire [3:3] \Командный_регистр_q_3 ;
  wire [5:0] bit_extender_1_out;
  wire [6:3] \Командный_регистр_q ;
  wire [7:0] adder_1_out, adder_2_out, adder_3_out, JR_q, not_2_out, pull_resistor_1_node,
       pull_resistor_2_node, R0_q, R2_q, R3_q, R4_q, ram_1_data, RTSK_q, \Адресный_регистр_q , \Регистр_0_q ,
       \сдвигатель_1_шина_2 , \Счетчик_команд_2_q ;
  wire [15:0] bit_extender_2_out, divider_1_out, divider_1_rem, divider_2_out, divider_2_rem, divider_3_out,
       divider_3_rem, divider_4_out, divider_4_rem, register_1_q;
  wire [15:8] R1_q;
  wire [17:0] rom_1_data;

  Counter #(.width(3), .max('h5), .trigger("falling")) \u_Счетчик_команд  (
    .Q(\Счетчик_команд_q ), .clk(\Тактовый_генератор_out ), .clr(\Сброс ));  // open: load, D, count, carry
  Counter \u_Счетчик_команд_2  (
    .load(rom_1_data[0]), .D(out_2), .count(rom_1_data[14]), .Q(\Счетчик_команд_2_q ),
    .clk(\Тактовый_генератор_out ), .clr(\Сброс ));  // open: carry
  Register \u_Командный_регистр  (
    .D(out_2), .en(rom_1_data[13]),
    .Q({\Командный_регистр_q , \Командный_регистр_q_3 [3], \Командный_регистр_q_2 }),
    .clk(\Тактовый_генератор_out ), .clr(\Сброс ));
  \Сдвигатель  \u_сдвигатель_1  (.\Шина (\Командный_регистр_q_2 ), .\Шина_2 (\сдвигатель_1_шина_2 ));
  Pull_Resistor pull_resistor_1 (.node(pull_resistor_1_node));
  assign pull_resistor_1_node = rom_1_data[7] ? \сдвигатель_1_шина_2  : 8'bz;  // Controlled_Buffer controlled_buffer_1
  \Компаратор  \u_компаратор_1  (
    .\Шина ({8{1'b1}}),
    .\Шина_2 ({\Командный_регистр_q , \Командный_регистр_q_3 [3], \Командный_регистр_q_2 }),
    .out_4(\компаратор_1_out_4 ));  // open: out_3, out_5
  not not_1 (not_1_out, \компаратор_1_out_4 );
  assign out_2 = rom_1_data[15] ? \Счетчик_команд_2_q  : 8'bz;  // Controlled_Buffer controlled_buffer_2
  Pull_Resistor pull_resistor_2 (.node(pull_resistor_2_node));
  assign pull_resistor_2_node = rom_1_data[8] ? \сдвигатель_1_шина_2  : 8'bz;  // Controlled_Buffer controlled_buffer_3
  ROM #(.addrWidth(7), .dataWidth(18)) rom_1 (
    .addr({\Командный_регистр_q , \Счетчик_команд_q }), .data(rom_1_data));  // open: sel
  Bit_Extender #(.out_width(6)) bit_extender_1 (.in(pull_resistor_2_node), .out(bit_extender_1_out));
  Clock \u_Тактовый_генератор  (.out(\Тактовый_генератор_out ));
  assign out_2 = rom_1_data[12] ? {\Командный_регистр_q , \Командный_регистр_q_3 [3], \Командный_регистр_q_2 } : 8'bz;  // Controlled_Buffer controlled_buffer_4
  Pull_Resistor pull_resistor_3 (.node(\Тактовый_генератор_out ));
  Pull_Resistor pull_resistor_4 (.node(\Сброс ));
  Pull_Resistor pull_resistor_5 (.node(out_2));
  assign out_2 = pull_resistor_1_node[1] ? R0_q : 8'bz;  // Controlled_Buffer controlled_buffer_5
  assign bit_extender_2_out = {{15{1'b0}}, \Тактовый_генератор_out };  // Bit_Extender bit_extender_2
  Counter #(.width(16), .max('hffff), .ongoal("continue")) \u_Счетчик_тактов  (
    .D(bit_extender_2_out), .count(not_1_out), .clk(\Тактовый_генератор_out ), .clr(\Сброс ));  // open: load, Q, carry
  Register \u_Адресный_регистр  (
    .D(out_2), .en(rom_1_data[11]), .Q(\Адресный_регистр_q ), .clk(\Тактовый_генератор_out ), .clr(\Сброс ));
  Register \u_Регистр_0  (
    .D(out_2), .en(bit_extender_1_out[0]), .Q(\Регистр_0_q ), .clk(\Тактовый_генератор_out ), .clr(\Сброс ));
  Adder adder_1 (.a(\Регистр_0_q ), .b(R0_q), .out(adder_1_out));  // open: cin, cout
  Register R0 (.D(out_2), .en(bit_extender_1_out[1]), .Q(R0_q), .clk(\Тактовый_генератор_out ), .clr(\Сброс ));
  Register R1 (.D(out_2), .en(bit_extender_1_out[2]), .Q(R1_q), .clk(\Тактовый_генератор_out ), .clr(\Сброс ));
  Register R3 (.D(out_2), .en(bit_extender_1_out[4]), .Q(R3_q), .clk(\Тактовый_генератор_out ), .clr(\Сброс ));
  Register R4 (.D(out_2), .en(bit_extender_1_out[5]), .Q(R4_q), .clk(\Тактовый_генератор_out ), .clr(\Сброс ));
  Register JR (.D(out_2), .en(rom_1_data[5]), .Q(JR_q), .clk(\Тактовый_генератор_out ), .clr(\Сброс ));
  assign out_2 = or_1_out ? JR_q : 8'bz;  // Controlled_Buffer controlled_buffer_6
  and and_1 (and_1_out, ~or_1_out, rom_1_data[4]);  // AND_Gate
  assign out_2 = and_1_out ? RTSK_q : 8'bz;  // Controlled_Buffer controlled_buffer_7
  assign out_2 = rom_1_data[10] ? ram_1_data : 8'bz;  // Controlled_Buffer controlled_buffer_8
  assign out_2 = pull_resistor_1_node[0] ? \Регистр_0_q  : 8'bz;  // Controlled_Buffer controlled_buffer_9
  assign out_2 = rom_1_data[6] ? adder_1_out : 8'bz;  // Controlled_Buffer controlled_buffer_10
  assign out_2 = pull_resistor_1_node[2] ? R1_q : 8'bz;  // Controlled_Buffer controlled_buffer_11
  assign out_2 = pull_resistor_1_node[3] ? R2_q : 8'bz;  // Controlled_Buffer controlled_buffer_12
  Register R2 (.D(out_2), .en(bit_extender_1_out[3]), .Q(R2_q), .clk(\Тактовый_генератор_out ), .clr(\Сброс ));
  assign out_2 = pull_resistor_1_node[4] ? R3_q : 8'bz;  // Controlled_Buffer controlled_buffer_13
  assign out_2 = pull_resistor_1_node[5] ? R4_q : 8'bz;  // Controlled_Buffer controlled_buffer_14
  and and_2 (and_2_out, rom_1_data[3], or_4_out);
  or or_1 (or_1_out, and_2_out, and_3_out);
  and and_3 (and_3_out, or_3_out, rom_1_data[2]);
  Register RTSK (.D(out_2), .en(rom_1_data[1]), .Q(RTSK_q), .clk(\Тактовый_генератор_out ), .clr(\Сброс ));
  or or_2 (or_2_out, rom_1_data[10], rom_1_data[9]);
  \Компаратор  \u_компаратор_2  (
    .\Шина (R1_q), .\Шина_2 (R2_q), .out_3(\компаратор_2_out_3 ), .out_4(\компаратор_2_out_4 ));  // open: out_5
  \Компаратор  \u_компаратор_3  (
    .\Шина (R3_q), .\Шина_2 (R4_q), .out_3(\компаратор_3_out_3 ), .out_4(\компаратор_3_out_4 ));  // open: out_5
  or or_3 (or_3_out, \компаратор_3_out_3 , \компаратор_3_out_4 );
  RAM #(.bus("separate")) ram_1 (
    .addr(\Адресный_регистр_q ), .din(out_2), .data(ram_1_data), .str(rom_1_data[9]), .sel(or_2_out),
    .clk(\Тактовый_генератор_out ), .ld(rom_1_data[10]));  // open: clr
  Adder adder_2 (.a(\Регистр_0_q ), .b(not_2_out), .out(adder_2_out));  // open: cin, cout
  assign not_2_out = ~R0_q;  // NOT_Gate not_2, 8 bits wide
  and and_4 (and_4_out, \компаратор_2_out_4 , \компаратор_3_out_3 );
  assign out_2 = rom_1_data[16] ? adder_3_out : 8'bz;  // Controlled_Buffer controlled_buffer_15
  Adder adder_3 (.a(adder_2_out), .b(8'h1), .out(adder_3_out));  // open: cin, cout
  or or_4 (or_4_out, \компаратор_2_out_3 , and_4_out);
  Hex_Digit_Display hex_digit_display_1 (.value(bit_extender_4_out));  // open: dp
  Hex_Digit_Display hex_digit_display_2 (.value(bit_extender_3_out));  // open: dp
  Bit_Extender #(.in_width(16), .out_width(4)) bit_extender_3 (.in(divider_1_out), .out(bit_extender_3_out));
  Divider #(.width(16)) divider_1 (
    .a(register_1_q), .b(16'h2710), .out(divider_1_out), .rem(divider_1_rem));  // open: upper
  Hex_Digit_Display hex_digit_display_3 (.value(bit_extender_6_out));  // open: dp
  Hex_Digit_Display hex_digit_display_4 (.value(bit_extender_5_out));  // open: dp
  Bit_Extender #(.in_width(16), .out_width(4)) bit_extender_4 (.in(divider_2_out), .out(bit_extender_4_out));
  Divider #(.width(16)) divider_2 (
    .a(divider_1_rem), .b(16'h3e8), .out(divider_2_out), .rem(divider_2_rem));  // open: upper
  Divider #(.width(16)) divider_3 (
    .a(divider_2_rem), .b(16'h64), .out(divider_3_out), .rem(divider_3_rem));  // open: upper
  Divider #(.width(16)) divider_4 (
    .a(divider_3_rem), .b(16'ha), .out(divider_4_out), .rem(divider_4_rem));  // open: upper
  Hex_Digit_Display hex_digit_display_5 (.value(bit_extender_7_out));  // open: dp
  Bit_Extender #(.in_width(16), .out_width(4)) bit_extender_5 (.in(divider_3_out), .out(bit_extender_5_out));
  Bit_Extender #(.in_width(16), .out_width(4)) bit_extender_6 (.in(divider_4_out), .out(bit_extender_6_out));
  Bit_Extender #(.in_width(16), .out_width(4)) bit_extender_7 (.in(divider_4_rem), .out(bit_extender_7_out));
  Register #(.width(16)) register_1 (
    .D({R1_q, R3_q}), .en(rom_1_data[17]), .Q(register_1_q), .clk(\Тактовый_генератор_out ), .clr(\Сброс ));

  // Notes on the sheet:
  //   contents of rom_1 (hex, n*v repeats v):
  //   4*0 8800 6400 0 0 8800 4500 880 500 8800 6400 0 0 8800 4500 0 0 8800 6400 0 0 8800 4402 810 280 8800
  //   6400 0 0 10100 0 0 0 8800 6400 0 0 140 0 0 0 8800 6400 0 0 8800 402 811 2400 8800 6400 0 0 8802 4420
  //   819 4000 8800 6400 0 0 8802 4420 815 4000 8800 6400 0 0 840 500 810 0 8800 6400 0 0 840 280 810 0
  //   8800 6400 0 0 20000 0 0 0 8800 6400 6*0 8800 6400
endmodule

// > = <
module \Компаратор  (
  input  [7:0] \Шина ,
  input  [7:0] \Шина_2 ,
  output out_3,
  output out_4,
  output out_5
);

  wire and_1_out, and_2_out, and_3_out, and_4_out, and_5_out, and_6_out, and_7_out, and_8_out, and_9_out,
       and_10_out, and_11_out, and_12_out, and_13_out, and_14_out, and_15_out, and_16_out, and_17_out,
       and_18_out, and_19_out, and_20_out, and_21_out, and_22_out, and_23_out, and_24_out, and_25_out,
       and_26_out, and_27_out, and_28_out, and_29_out, and_30_out, nor_1_out, nor_2_out, nor_3_out,
       nor_4_out, nor_5_out, nor_6_out, nor_7_out, nor_8_out, not_1_out, not_2_out, not_3_out, not_4_out,
       not_5_out, not_6_out, not_7_out, not_8_out, not_9_out, not_10_out, not_11_out, not_12_out, not_13_out,
       not_14_out, not_15_out, not_16_out;

  and and_1 (and_1_out, \Шина_2 [7], not_1_out);
  not not_1 (not_1_out, \Шина [7]);
  and and_2 (and_2_out, \Шина [7], not_2_out);
  not not_2 (not_2_out, \Шина_2 [7]);
  and and_3 (and_3_out, \Шина_2 [6], not_3_out);
  not not_3 (not_3_out, \Шина [6]);
  and and_4 (and_4_out, \Шина [6], not_4_out);
  not not_4 (not_4_out, \Шина_2 [6]);
  and and_5 (and_5_out, \Шина_2 [5], not_5_out);
  not not_5 (not_5_out, \Шина [5]);
  and and_6 (and_6_out, \Шина [5], not_6_out);
  not not_6 (not_6_out, \Шина_2 [5]);
  and and_7 (and_7_out, \Шина_2 [4], not_7_out);
  not not_7 (not_7_out, \Шина [4]);
  and and_8 (and_8_out, \Шина [4], not_8_out);
  not not_8 (not_8_out, \Шина_2 [4]);
  and and_9 (and_9_out, \Шина_2 [3], not_9_out);
  not not_9 (not_9_out, \Шина [3]);
  and and_10 (and_10_out, \Шина [3], not_10_out);
  not not_10 (not_10_out, \Шина_2 [3]);
  and and_11 (and_11_out, \Шина_2 [2], not_11_out);
  not not_11 (not_11_out, \Шина [2]);
  and and_12 (and_12_out, \Шина [2], not_12_out);
  not not_12 (not_12_out, \Шина_2 [2]);
  and and_13 (and_13_out, \Шина_2 [1], not_13_out);
  not not_13 (not_13_out, \Шина [1]);
  and and_14 (and_14_out, \Шина [1], not_14_out);
  not not_14 (not_14_out, \Шина_2 [1]);
  and and_15 (and_15_out, \Шина_2 [0], not_15_out);
  not not_15 (not_15_out, \Шина [0]);
  and and_16 (and_16_out, \Шина [0], not_16_out);
  not not_16 (not_16_out, \Шина_2 [0]);
  nor nor_1 (nor_1_out, and_9_out, and_10_out);
  nor nor_2 (nor_2_out, and_11_out, and_12_out);
  nor nor_3 (nor_3_out, and_13_out, and_14_out);
  nor nor_4 (nor_4_out, and_15_out, and_16_out);
  nor nor_5 (nor_5_out, and_1_out, and_2_out);
  nor nor_6 (nor_6_out, and_3_out, and_4_out);
  nor nor_7 (nor_7_out, and_5_out, and_6_out);
  nor nor_8 (nor_8_out, and_7_out, and_8_out);
  and and_17 (and_17_out, and_3_out, nor_5_out);
  and and_18 (and_18_out, nor_5_out, and_4_out);
  and and_19 (and_19_out, and_5_out, nor_5_out, nor_6_out);
  and and_20 (and_20_out, nor_5_out, nor_6_out, and_6_out);
  and and_21 (and_21_out, nor_5_out, nor_6_out, and_7_out, nor_7_out);
  and and_22 (and_22_out, nor_5_out, nor_6_out, nor_7_out, and_8_out);
  and and_23 (and_23_out, and_9_out, nor_5_out, nor_8_out, nor_6_out, nor_7_out);
  and and_24 (and_24_out, nor_5_out, nor_6_out, nor_7_out, nor_8_out, and_10_out);
  and and_25 (and_25_out, nor_5_out, nor_6_out, nor_7_out, nor_8_out, nor_1_out, and_11_out);
  and and_26 (and_26_out, nor_7_out, nor_5_out, nor_6_out, nor_1_out, and_12_out, nor_8_out);
  and and_27 (and_27_out, and_13_out, nor_6_out, nor_7_out, nor_5_out, nor_8_out, nor_1_out, nor_2_out);
  and and_28 (and_28_out, nor_6_out, nor_2_out, nor_1_out, nor_8_out, nor_7_out, nor_5_out, and_14_out);
  and and_29 (and_29_out, and_15_out, nor_5_out, nor_7_out, nor_1_out, nor_2_out, nor_3_out, nor_8_out, nor_6_out);
  and and_30 (and_30_out, nor_1_out, nor_5_out, nor_6_out, nor_7_out, nor_8_out, nor_2_out, nor_3_out, and_16_out);
  and and_31 (out_4, nor_5_out, nor_6_out, nor_7_out, nor_8_out, nor_1_out, nor_2_out, nor_3_out, nor_4_out);
  or or_1 (out_5, and_1_out, and_17_out, and_19_out, and_21_out, and_23_out, and_25_out, and_27_out, and_29_out);
  or or_2 (out_3, and_18_out, and_20_out, and_22_out, and_24_out, and_26_out, and_28_out, and_30_out, and_2_out);
endmodule

// <-
module \Сдвигатель  (
  input  [2:0] \Шина ,
  output [7:0] \Шина_2 
);

  wire \компаратор_1_out_4 , \компаратор_2_out_4 , \компаратор_3_out_4 , \компаратор_4_out_4 ,
       \компаратор_5_out_4 , \компаратор_6_out_4 , \компаратор_7_out_4 , \компаратор_8_out_4 ;
  wire [7:0] bit_extender_1_out;

  assign bit_extender_1_out = {{5{1'b0}}, \Шина };  // Bit_Extender bit_extender_1
  \Компаратор  \u_компаратор_1  (
    .\Шина (bit_extender_1_out), .\Шина_2 ({8{1'b0}}), .out_4(\компаратор_1_out_4 ));  // open: out_3, out_5
  assign \Шина_2  = \компаратор_1_out_4  ? 8'h1 : 8'bz;  // Controlled_Buffer controlled_buffer_1
  assign \Шина_2  = \компаратор_2_out_4  ? 8'h2 : 8'bz;  // Controlled_Buffer controlled_buffer_2
  \Компаратор  \u_компаратор_2  (
    .\Шина (bit_extender_1_out), .\Шина_2 (8'h1), .out_4(\компаратор_2_out_4 ));  // open: out_3, out_5
  assign \Шина_2  = \компаратор_3_out_4  ? 8'h4 : 8'bz;  // Controlled_Buffer controlled_buffer_3
  \Компаратор  \u_компаратор_3  (
    .\Шина (bit_extender_1_out), .\Шина_2 (8'h2), .out_4(\компаратор_3_out_4 ));  // open: out_3, out_5
  assign \Шина_2  = \компаратор_4_out_4  ? 8'h8 : 8'bz;  // Controlled_Buffer controlled_buffer_4
  \Компаратор  \u_компаратор_4  (
    .\Шина (bit_extender_1_out), .\Шина_2 (8'h3), .out_4(\компаратор_4_out_4 ));  // open: out_3, out_5
  assign \Шина_2  = \компаратор_5_out_4  ? 8'h10 : 8'bz;  // Controlled_Buffer controlled_buffer_5
  \Компаратор  \u_компаратор_5  (
    .\Шина (bit_extender_1_out), .\Шина_2 (8'h4), .out_4(\компаратор_5_out_4 ));  // open: out_3, out_5
  assign \Шина_2  = \компаратор_6_out_4  ? 8'h20 : 8'bz;  // Controlled_Buffer controlled_buffer_6
  \Компаратор  \u_компаратор_6  (
    .\Шина (bit_extender_1_out), .\Шина_2 (8'h5), .out_4(\компаратор_6_out_4 ));  // open: out_3, out_5
  assign \Шина_2  = \компаратор_7_out_4  ? 8'h40 : 8'bz;  // Controlled_Buffer controlled_buffer_7
  \Компаратор  \u_компаратор_7  (
    .\Шина (bit_extender_1_out), .\Шина_2 (8'h6), .out_4(\компаратор_7_out_4 ));  // open: out_3, out_5
  assign \Шина_2  = \компаратор_8_out_4  ? 8'h80 : 8'bz;  // Controlled_Buffer controlled_buffer_8
  \Компаратор  \u_компаратор_8  (
    .\Шина (bit_extender_1_out), .\Шина_2 (8'h7), .out_4(\компаратор_8_out_4 ));  // open: out_3, out_5
endmodule
