// Logisim project ready.circ as structural Verilog: 1 circuit, main circuit main
module main (
  input  \Сброс ,
  input  \Очистка_ОЗУ ,
  output [7:0] out_3
);

  wire and_1_out, and_2_out, clock_1_out, not_1_out, or_1_out, or_2_out, or_3_out, pull_resistor_1_node,
       pull_resistor_4_node, \Рег__флага_нуля_q ;
  wire [2:0] \Сч__шага_q ;
  wire [3:0] bit_extender_1_out, bit_extender_3_out, bit_extender_5_out, bit_extender_6_out,
       bit_extender_7_out, bit_extender_8_out, \Адр__Рег_q , \Счётчик_команд_q ;
  wire [7:0] adder_1_out, bit_extender_2_out, bit_extender_4_out, controlled_buffer_5_out, divider_1_out,
       divider_1_rem, divider_2_out, divider_2_rem, pull_resistor_2_node, pull_resistor_5_node, register_1_q,
       xnor_1_out, xor_1_out, \Ком__Рег_q , \РОН_А_q , \РОН_Б_q ;
  wire [7:7] rom_1_data_2;
  wire [14:0] rom_1_data;

  and and_1 (and_1_out, or_1_out, pull_resistor_4_node);
  or or_1 (or_1_out, rom_1_data[7], rom_1_data[8], rom_1_data[10]);
  Pull_Resistor pull_resistor_1 (.node(pull_resistor_1_node));
  assign pull_resistor_1_node = and_1_out ? rom_1_data[10] : 1'bz;  // Controlled_Buffer controlled_buffer_1
  Bit_Extender #(.out_width(4)) bit_extender_1 (.in(pull_resistor_2_node), .out(bit_extender_1_out));
  Counter #(.width(4), .max('hf)) \u_Счётчик_команд  (
    .load(pull_resistor_1_node), .D(bit_extender_1_out), .count(rom_1_data[9]), .Q(\Счётчик_команд_q ),
    .clk(clock_1_out), .clr(\Сброс ));  // open: carry
  Pull_Resistor pull_resistor_2 (.node(pull_resistor_2_node));
  Register \u_Ком__Рег  (.D(out_3), .en(rom_1_data[4]), .Q(\Ком__Рег_q ), .clk(clock_1_out), .clr(\Сброс ));
  Counter #(.width(3), .max('h7), .ongoal("load")) \u_Сч__шага  (
    .Q(\Сч__шага_q ), .clk(not_1_out), .clr(or_2_out));  // open: load, D, count, carry
  buf or_2 (or_2_out, \Сброс );  // OR_Gate
  assign bit_extender_2_out = {{4{1'b0}}, \Счётчик_команд_q };  // Bit_Extender bit_extender_2
  Bit_Extender #(.out_width(4)) bit_extender_3 (.in(\Ком__Рег_q ), .out(bit_extender_3_out));
  not not_1 (not_1_out, clock_1_out);
  assign out_3 = rom_1_data[7] ? bit_extender_2_out : 8'bz;  // Controlled_Buffer controlled_buffer_2
  assign out_3 = rom_1_data[3] ? bit_extender_4_out : 8'bz;  // Controlled_Buffer controlled_buffer_3
  assign bit_extender_4_out = {{4{1'b0}}, bit_extender_3_out};  // Bit_Extender bit_extender_4
  assign pull_resistor_2_node = and_1_out ? out_3 : 8'bz;  // Controlled_Buffer controlled_buffer_4
  ROM #(.addrWidth(7), .dataWidth(15)) rom_1 (
    .addr({\Ком__Рег_q [7:4], \Сч__шага_q }), .data({rom_1_data[14:13], rom_1_data_2[7], rom_1_data[11:0]}));  // open: sel
  Clock clock_1 (.out(clock_1_out));
  Pull_Resistor pull_resistor_3 (.node(out_3));
  Pull_Resistor #(.pull(1)) pull_resistor_4 (.node(pull_resistor_4_node));
  assign controlled_buffer_5_out = and_1_out ? out_3 : 8'bz;  // Controlled_Buffer controlled_buffer_5
  assign out_3 = rom_1_data[0] ? adder_1_out : 8'bz;  // Controlled_Buffer controlled_buffer_6
  assign out_3 = rom_1_data[11] ? \РОН_А_q  : 8'bz;  // Controlled_Buffer controlled_buffer_7
  Register \u_РОН_А  (.D(out_3), .en(rom_1_data[2]), .Q(\РОН_А_q ), .clk(clock_1_out), .clr(\Сброс ));
  Register \u_РОН_Б  (.D(out_3), .en(rom_1_data[1]), .Q(\РОН_Б_q ), .clk(clock_1_out), .clr(\Сброс ));
  Bit_Extender #(.out_width(4)) bit_extender_5 (.in(controlled_buffer_5_out), .out(bit_extender_5_out));
  Adder adder_1 (.a(\РОН_А_q ), .b(xor_1_out), .out(adder_1_out), .cin(rom_1_data_2[7]));  // open: cout
  assign xor_1_out = \РОН_Б_q  ^ {8{rom_1_data_2[7]}};  // XOR_Gate xor_1, 8 bits wide
  Register #(.width(4)) \u_Адр__Рег  (
    .D(bit_extender_5_out), .en(rom_1_data[8]), .Q(\Адр__Рег_q ), .clk(clock_1_out), .clr(\Сброс ));
  Pull_Resistor pull_resistor_5 (.node(pull_resistor_5_node));
  assign xnor_1_out = ~(adder_1_out ^ pull_resistor_5_node);  // XNOR_Gate xnor_1, 8 bits wide
  or or_3 (or_3_out, rom_1_data[6], rom_1_data[5]);
  RAM #(.addrWidth(4), .bus("separate")) ram_1 (
    .addr(\Адр__Рег_q ), .din(out_3), .data(out_3), .str(rom_1_data[5]), .sel(or_3_out), .clk(clock_1_out),
    .ld(rom_1_data[6]), .clr(\Очистка_ОЗУ ));
  assign pull_resistor_4_node = rom_1_data[14] ? ~\Рег__флага_нуля_q  : 1'bz;  // Controlled_Inverter controlled_inverter_1
  Register #(.width(1)) \u_Рег__флага_нуля  (
    .D(and_2_out), .en(rom_1_data[13]), .Q(\Рег__флага_нуля_q ), .clk(clock_1_out), .clr(\Сброс ));
  and and_2 (and_2_out, xnor_1_out[0], xnor_1_out[1], xnor_1_out[2], xnor_1_out[3], xnor_1_out[4], xnor_1_out[5], xnor_1_out[6], xnor_1_out[7]);
  Register register_1 (.D(out_3), .Q(register_1_q), .clk(clock_1_out));  // open: en, clr
  Divider divider_1 (.a(register_1_q), .b(8'h64), .out(divider_1_out), .rem(divider_1_rem));  // open: upper
  Divider divider_2 (.a(divider_1_rem), .b(8'ha), .out(divider_2_out), .rem(divider_2_rem));  // open: upper
  Bit_Extender #(.out_width(4)) bit_extender_6 (.in(divider_1_out), .out(bit_extender_6_out));
  Bit_Extender #(.out_width(4)) bit_extender_7 (.in(divider_2_out), .out(bit_extender_7_out));
  Bit_Extender #(.out_width(4)) bit_extender_8 (.in(divider_2_rem), .out(bit_extender_8_out));
  Hex_Digit_Display hex_digit_display_1 (.value(bit_extender_6_out));  // open: dp
  Hex_Digit_Display hex_digit_display_2 (.value(bit_extender_7_out));  // open: dp
  Hex_Digit_Display hex_digit_display_3 (.value(bit_extender_8_out));  // open: dp

  // Notes on the sheet:
  //   ПЗУ (Декодер)
  //   Вых. сч. ком.
  //   Очистка сч. ком.
  //   Такт. вх. сч. ком.
  //   Вх. сч. ком.
  //   Вых. ком. рег.
  //   Вх. ком. рег.
  //   Очистка ком. рег.
  //   Такт. вх. ком. рег.
  //   Очистка сч. ком.
  //   Такт. вх. сч. ком.
  //   contents of rom_1 (hex, n*v repeats v):
  //   180 50 108 44 200 0 0 0 180 50 108 42 5 200 0 0 180 50 108 820 200 0 0 0 180 50 108 42 1005 200 0 0
  //   180 50 c 200 4*0 180 50 140 42 3001 200 0 0 180 50 4540 200 68*0 180 50 4000
  //   Сум.
  //   Вх. рег. Б
  //   Вх. рег. А
  //   Вых. ком. рег.
  //   Вх. ком. рег.
  //   Зап. ОЗУ
  //   Чт. ОЗУ
  //   Вх. адр. рег.
  //   Вых. сч. ком.
  //   Напр. сч.
  //   Загр. сч.
  //   Вых. рег. А
  //   Доп. Код
  //   Вх. рег. флага 0
  //   Запись в ОЗУ с шины
  //   Загр. знач. адр. рег.
  //   Такт. вх. адр. рег.
  //   Очистка адр. рег.
  //   Такт. вх. ОЗУ
  //   Вых. Сум.
  //   Вых. А
  //   Вх. данных А
  //   Такт. А
  //   Сброс А
  //   Вх. данных Б
  //   Такт. Б
  //   Сброс Б
  //   Значения, счит. по адр. ОЗУ
  //   ОЗУ
endmodule
