// Logisim project Сдвиг на 1 бит влево для 4 бит.circ as structural Verilog: 1 circuit, main circuit main
module main (
  input  [2:0] in_1,
  output [7:0] \Шина 
);

  wire bitselector_1_out, bitselector_2_out, bitselector_3_out;
  wire [4:0] adder_1_out, adder_2_out, adder_3_out, adder_4_out, adder_5_out, bit_extender_1_out,
       bit_extender_2_out, bit_extender_3_out, controlled_buffer_1_out, controlled_buffer_2_out,
       controlled_buffer_3_out;

  BitSelector #(.width(3)) bitselector_1 (.in(in_1), .out(bitselector_1_out), .sel(2'b00));
  BitSelector #(.width(3)) bitselector_2 (.in(in_1), .out(bitselector_2_out), .sel(2'b01));
  BitSelector #(.width(3)) bitselector_3 (.in(in_1), .out(bitselector_3_out), .sel(2'b10));
  assign bit_extender_1_out = {{4{1'b0}}, bitselector_1_out};  // Bit_Extender bit_extender_1
  assign bit_extender_2_out = {{4{1'b0}}, bitselector_2_out};  // Bit_Extender bit_extender_2
  assign bit_extender_3_out = {{4{1'b0}}, bitselector_3_out};  // Bit_Extender bit_extender_3
  Adder #(.width(5)) adder_1 (
    .a(bit_extender_1_out), .b(controlled_buffer_1_out), .out(adder_1_out));  // open: cin, cout
  assign controlled_buffer_1_out = bitselector_1_out ? 5'b00001 : 5'bz;  // Controlled_Buffer controlled_buffer_1
  Pull_Resistor pull_resistor_1 (.node(adder_1_out));
  Adder #(.width(5)) adder_2 (
    .a(bit_extender_2_out), .b(controlled_buffer_2_out), .out(adder_2_out));  // open: cin, cout
  assign controlled_buffer_2_out = bitselector_2_out ? 5'b00011 : 5'bz;  // Controlled_Buffer controlled_buffer_2
  Pull_Resistor pull_resistor_2 (.node(adder_2_out));
  Adder #(.width(5)) adder_3 (
    .a(bit_extender_3_out), .b(controlled_buffer_3_out), .out(adder_3_out));  // open: cin, cout
  assign controlled_buffer_3_out = bitselector_3_out ? 5'b00111 : 5'bz;  // Controlled_Buffer controlled_buffer_3
  Pull_Resistor pull_resistor_3 (.node(adder_3_out));
  Adder #(.width(5)) adder_4 (.a(adder_1_out), .b(adder_2_out), .out(adder_4_out));  // open: cin, cout
  Adder #(.width(5)) adder_5 (.a(adder_4_out), .b(adder_3_out), .out(adder_5_out));  // open: cin, cout
  assign \Шина  = {{3{1'b0}}, adder_5_out};  // Bit_Extender bit_extender_4
endmodule
